# Fritzing sketch tutorial (saved by Fritzing 0.9.2b)
circuit board: 8.53488cm x 5.63626cm
breadboards: 1

parts:
  R1 = Resistor [tolerance=±5% resistance=4.7k package=THT]
  DHT1 = DHT11 Humitidy and Temperature Sensor
  DS1 = DS18B20 1-Wire Temperature Sensor [part_number=DS18B20]
  R3 = Resistor [tolerance=±5% resistance=4.7k package=THT]
  Raspberry_Pi1 = Raspberry Pi 2
  LED1 = LED - 3mm [color="Red (633nm)" package="3 mm [THT]"]
  R4 = Resistor [tolerance=±5% resistance=220 package=THT]

nets:
  N1: R1.Pin_0, DS1.DQ, Raspberry_Pi1.GPIO4
  VDD: R1.Pin_1, DHT1.VDD, DS1.VDD, R3.Pin_1, Raspberry_Pi1.3v3, Raspberry_Pi1.3V3
  N2: DHT1.DATA, R3.Pin_0, Raspberry_Pi1.GPIO6
  GND: DHT1.GND, DS1.GND, Raspberry_Pi1.GND, R4.Pin_1
  N3: Raspberry_Pi1.GPIO19, LED1.anode
  N4: LED1.cathode, R4.Pin_0

custom parts:
  DHT11 Humitidy and Temperature Sensor: DHT11 Humidity and Temperature Sensor
